# Fritzing sketch ArduinoMKRWifi1010_2NeopixelStrip (saved by Fritzing 0.9.3b)
breadboards: 1

parts:
  Mod1 = Arduino MKR Wifi 1010
  Strip1_-_Neopixel/WS2812B_30_pixels = Neopixel Strip -- Black (30/m)
  Strip2_-_Neopixel/WS2812B_30_pixels = Neopixel Strip -- Black (30/m)

nets:
  GND: Mod1.GND, Strip1_-_Neopixel/WS2812B_30_pixels.GND, Strip2_-_Neopixel/WS2812B_30_pixels.GND
  N1: Mod1.~D4, Strip2_-_Neopixel/WS2812B_30_pixels.Din
  N2: Mod1.~D5, Strip1_-_Neopixel/WS2812B_30_pixels.Din
  +5V: Mod1.+5V, Strip1_-_Neopixel/WS2812B_30_pixels.+5V, Strip2_-_Neopixel/WS2812B_30_pixels.+5V

custom parts:
  Arduino MKR Wifi 1010: Arduino MKR Wifi 1010, SAMD21 Cortex-M0+ 32bit Low Power ARM MCU,Flash Memory 256 KB, SRAM 32KB, 48mhz clock, Ublok Wifi interface.
  Neopixel Strip -- Black (30/m): These NeoPixel strips have 30 digitally-addressable pixel LEDs per meter and are very affordable and are only 12.5 mm wide, 10 mm if you remove the strip from the casing.
